# Fritzing sketch esp01_btns (saved by Fritzing 0.9.3b)
circuit board: 2.5834cm x 1.77056cm

parts:
  U1 = ESP8266 WiFi Module [part_number=ESP8266]
  S5 = Momentary Switch [package=ksa_sealed_tac_switch]
  S4 = Momentary Switch [package=ksa_sealed_tac_switch]

nets:
  N1: U1.GPIO_0, S5.3, S5.4
  N2: U1.RST, S4.3, S4.4
  N3: U1.GND, S5.1, S5.2, S4.1, S4.2

notes:
  RESET
  PROGRAM

custom parts:
  ESP8266 WiFi Module: Generic WiFi Module based on the ESP8266 with onboard PCB antenna and UART communications
